// Logisim project Problema1a-Conversor_Gray-Binario.circ as structural Verilog: 1 circuit, main circuit main
module main (
  input  [3:0] BITS_GRAY,
  output out_2,
  output BITS_BINARIO,
  output out_4,
  output out_5
);

  xor xor_1 (BITS_BINARIO, BITS_GRAY[3], BITS_GRAY[2]);
  xor xor_2 (out_4, BITS_BINARIO, BITS_GRAY[1]);
  xor xor_3 (out_5, out_4, BITS_GRAY[0]);

  assign out_2 = BITS_GRAY[3];

  // Notes on the sheet:
  //   Conversor de Gray a Binario
endmodule
