// Logisim project Problema1b-Conversor_Doble.circ as structural Verilog: 1 circuit, main circuit main
module main (
  input  [3:0] in_1,
  input  Bit_de_control,
  output out_3,
  output out_4,
  output out_5,
  output out_6
);

  wire multiplexer_1_out, multiplexer_2_out;

  xor xor_1 (out_4, in_1[3], in_1[2]);
  Multiplexer multiplexer_1 (.in0(out_4), .in1(in_1[2]), .out(multiplexer_1_out), .sel(Bit_de_control));  // open: en
  xor xor_2 (out_5, multiplexer_1_out, in_1[1]);
  Multiplexer multiplexer_2 (.in0(out_5), .in1(in_1[1]), .out(multiplexer_2_out), .sel(Bit_de_control));  // open: en
  xor xor_3 (out_6, multiplexer_2_out, in_1[0]);

  assign out_3 = in_1[3];

  // Notes on the sheet:
  //   0 = Gray -> Binario
  //   1 = Binario -> Gray
endmodule
