// Logisim project Problema2-Circuito_simplificado.circ as structural Verilog: 1 circuit, main circuit main
module main (
  input  X,
  input  Y,
  input  Z,
  output F
);

  wire nand_1_out, nand_2_out, nand_3_out, nand_4_out;

  nand nand_1 (nand_1_out, X, X);
  nand nand_2 (nand_2_out, Y, Y);
  nand nand_3 (nand_3_out, nand_1_out, nand_2_out);
  nand nand_4 (nand_4_out, nand_3_out, Z);
  nand nand_5 (F, nand_4_out, nand_4_out);

  // Notes on the sheet:
  //   ~X
  //   ~Y
  //   ~(~X*~Y) == X+Y
  //   ~(Z*(X+Y))
  //   Z*(X+Y)
endmodule
