// Logisim project Problema3b1-Circuito_Puertas_Cualesquiera_2_Entradas.circ as structural Verilog: 1 circuit, main circuit main
module main (
  input  A,
  input  B,
  input  C,
  input  A_2,
  input  B_2,
  input  C_2,
  output out_7,
  output out_8
);

  wire and_1_out, and_2_out, and_3_out, and_4_out, and_5_out, not_1_out, not_2_out, or_1_out;

  not not_1 (not_1_out, B);
  not not_2 (not_2_out, C);
  and and_1 (and_1_out, A, C);
  and and_2 (and_2_out, not_1_out, not_2_out);
  and and_3 (and_3_out, A_2, B_2);
  and and_4 (and_4_out, B_2, C_2);
  and and_5 (and_5_out, A_2, C_2);
  or or_1 (or_1_out, and_3_out, and_4_out);
  or or_2 (out_7, and_1_out, and_2_out);
  or or_3 (out_8, or_1_out, and_5_out);

  // Notes on the sheet:
  //   PUERTAS CUALESQUIERA
  //   F(A,B,C)
  //   G(A,B,C)
endmodule
