// Logisim project Problema3b2-Circuito_Puertas_AND.circ as structural Verilog: 1 circuit, main circuit main
module main (
  input  A,
  input  B,
  input  C,
  input  A_2,
  input  B_2,
  input  C_2,
  output F,
  output G
);

  wire and_1_out, and_2_out, and_3_out, and_4_out, and_5_out, and_6_out, and_7_out, and_8_out, not_1_out,
       not_2_out, not_3_out, not_4_out, not_5_out, not_6_out, not_7_out;

  not not_1 (not_1_out, B);
  not not_2 (not_2_out, C);
  and and_1 (and_1_out, A, C);
  and and_2 (and_2_out, not_1_out, not_2_out);
  and and_3 (and_3_out, A_2, C_2);
  and and_4 (and_4_out, A_2, B_2);
  and and_5 (and_5_out, B_2, C_2);
  not not_3 (not_3_out, and_1_out);
  not not_4 (not_4_out, and_2_out);
  not not_5 (not_5_out, and_3_out);
  not not_6 (not_6_out, and_4_out);
  not not_7 (not_7_out, and_5_out);
  and and_6 (and_6_out, not_3_out, not_4_out);
  and and_7 (and_7_out, not_5_out, not_6_out);
  and and_8 (and_8_out, and_7_out, not_7_out);
  not not_8 (F, and_6_out);
  not not_9 (G, and_8_out);

  // Notes on the sheet:
  //   PUERTAS AND DE 2 ENTRADAS:
  //   ~B
  //   ~C
  //   A*C
  //   ~B*~C
  //   A*C
  //   A*B
  //   B*C
  //   F(A,B,C)
  //   ~(A*C)
  //   ~(~B*~C)
  //   G(A,B,C)
  //   ~(A*C)
  //   ~(A*B)
  //   ~(B*C)
  //   ~(A*C)*~(~B*~C)
  //   ~(A*C)*~(A*B)
  //   ~(~(A*C)*~(~B*~C))
  //   ~(A*C)*~(A*B)*~(B*C)
  //   ~(~(A*C)*~(A*B)*~(B*C))
endmodule
