// Logisim project Problema3b3-Circuito_Puertas_NAND.circ as structural Verilog: 1 circuit, main circuit main
module main (
  input  A,
  input  B,
  input  C,
  input  A_2,
  input  B_2,
  input  C_2,
  output F,
  output G
);

  wire nand_1_out, nand_2_out, nand_3_out, nand_4_out, nand_5_out, nand_6_out, nand_7_out, nand_8_out,
       nand_10_out;

  nand nand_1 (nand_1_out, A, C);
  nand nand_2 (nand_2_out, B, B);
  nand nand_3 (nand_3_out, C, C);
  nand nand_4 (nand_4_out, A_2, C_2);
  nand nand_5 (nand_5_out, A_2, B_2);
  nand nand_6 (nand_6_out, B_2, C_2);
  nand nand_7 (nand_7_out, nand_2_out, nand_3_out);
  nand nand_8 (nand_8_out, nand_4_out, nand_5_out);
  nand nand_9 (F, nand_1_out, nand_7_out);
  nand nand_10 (nand_10_out, nand_8_out, nand_8_out);
  nand nand_11 (G, nand_10_out, nand_6_out);

  // Notes on the sheet:
  //   PUERTAS NAND DE 2 ENTRADAS:
  //   ~B
  //   ~(A*C)
  //   ~C
  //   ~(A*C)
  //   ~(A*B)
  //   ~(B*C)
  //   F(A,B,C)
  //   ~(~B*~C)
  //   G(A,B,C)
  //   ~(~(A*C)*~(A*B))
  //   ~(~(A*C)*~(~B*~C))
  //   ~(A*C)*~(A*B)
  //   ~(~(A*C)*~(A*B)*~(B*C))
endmodule
