// Logisim project Problema4-Simulacion_desplazador.circ as structural Verilog: 1 circuit, main circuit main
module main (
  input  E3,
  input  E2,
  input  E1,
  input  E0,
  input  [1:0] S1_S0,
  output out_6,
  output out_7,
  output out_8,
  output out_9
);

  Multiplexer #(.select(2)) multiplexer_1 (.in0(E3), .in1(E0), .in2(E1), .in3(E2), .out(out_6), .sel(S1_S0), .en(1'b1));
  Multiplexer #(.select(2)) multiplexer_2 (.in0(E2), .in1(E3), .in2(E0), .in3(E1), .out(out_7), .sel(S1_S0), .en(1'b1));
  Multiplexer #(.select(2)) multiplexer_3 (.in0(E1), .in1(E2), .in2(E3), .in3(E0), .out(out_8), .sel(S1_S0), .en(1'b1));
  Multiplexer #(.select(2)) multiplexer_4 (.in0(E0), .in1(E1), .in2(E2), .in3(E3), .out(out_9), .sel(S1_S0), .en(1'b1));

  // Notes on the sheet:
  //   S1=0, S0=0 -> Retener bits
  //   S1=0, S0=1 -> Desplazar un bit a la derecha
  //   S1=1, S0=0 -> Desplazar dos bits a la derecha
  //   S1=1, S0=1 -> Desplazar un bit a la izquierda
  //   G3
  //   G2
  //   G1
  //   G0
endmodule
