// Logisim project Problema1-Restador.circ as structural Verilog: 4 circuits, main circuit main
module main (
  input  [5:0] A,
  input  [5:0] B,
  output R,
  output out_4,
  output out_5,
  output out_6,
  output out_7,
  output out_8
);

  wire complemento_a_2_1_out_7, complemento_a_2_1_out_8, complemento_a_2_1_out_9, complemento_a_2_1_out_10,
       complemento_a_2_1_out_11, complemento_a_2_1_out_12;

  Complemento_a_2 complemento_a_2_1 (
    .in_1(B[0]), .in_2(B[1]), .in_3(B[2]), .in_4(B[3]), .in_5(B[4]), .in_6(B[5]),
    .out_7(complemento_a_2_1_out_7), .out_8(complemento_a_2_1_out_8), .out_9(complemento_a_2_1_out_9),
    .out_10(complemento_a_2_1_out_10), .out_11(complemento_a_2_1_out_11), .out_12(complemento_a_2_1_out_12));
  Sumador_6_bits sumador_6_bits_1 (
    .A0(A[0]), .B0(complemento_a_2_1_out_7), .A1(A[1]), .B1(complemento_a_2_1_out_8), .A2(A[2]),
    .B2(complemento_a_2_1_out_9), .A3(A[3]), .B3(complemento_a_2_1_out_10), .A4(A[4]),
    .B4(complemento_a_2_1_out_11), .A5(A[5]), .B5(complemento_a_2_1_out_12), .S0(out_8), .S1(out_7),
    .S2(out_6), .S3(out_5), .S4(out_4), .S5(R));

  // Notes on the sheet:
  //   Restador:
endmodule

module Complemento_a_2 (
  input  in_1,
  input  in_2,
  input  in_3,
  input  in_4,
  input  in_5,
  input  in_6,
  output out_7,
  output out_8,
  output out_9,
  output out_10,
  output out_11,
  output out_12
);

  wire not_1_out, not_2_out, not_3_out, not_4_out, not_5_out, not_6_out;

  not not_1 (not_1_out, in_1);
  not not_2 (not_2_out, in_2);
  not not_3 (not_3_out, in_3);
  not not_4 (not_4_out, in_4);
  not not_5 (not_5_out, in_5);
  not not_6 (not_6_out, in_6);
  Sumador_6_bits sumador_6_bits_1 (
    .A0(not_1_out), .B0(1'b1), .A1(not_2_out), .B1(1'b0), .A2(not_3_out), .B2(1'b0), .A3(not_4_out),
    .B3(1'b0), .A4(not_5_out), .B4(1'b0), .A5(not_6_out), .B5(1'b0), .S0(out_7), .S1(out_8), .S2(out_9),
    .S3(out_10), .S4(out_11), .S5(out_12));

  // Notes on the sheet:
  //   Complemento a 2
endmodule

module Sumador_6_bits (
  input  A0,
  input  B0,
  input  A1,
  input  B1,
  input  A2,
  input  B2,
  input  A3,
  input  B3,
  input  A4,
  input  B4,
  input  A5,
  input  B5,
  output S0,
  output S1,
  output S2,
  output S3,
  output S4,
  output S5
);

  wire sumador_1_cout, sumador_2_cout, sumador_3_cout, sumador_4_cout, sumador_5_cout;

  Sumador sumador_1 (.A(A0), .B(B0), .Cin(1'b0), .Cout(sumador_1_cout), .S(S0));
  Sumador sumador_2 (.A(A1), .B(B1), .Cin(sumador_1_cout), .Cout(sumador_2_cout), .S(S1));
  Sumador sumador_3 (.A(A2), .B(B2), .Cin(sumador_2_cout), .Cout(sumador_3_cout), .S(S2));
  Sumador sumador_4 (.A(A3), .B(B3), .Cin(sumador_3_cout), .Cout(sumador_4_cout), .S(S3));
  Sumador sumador_5 (.A(A4), .B(B4), .Cin(sumador_4_cout), .Cout(sumador_5_cout), .S(S4));
  Sumador sumador_6 (.A(A5), .B(B5), .Cin(sumador_5_cout), .S(S5));  // open: Cout

  // Notes on the sheet:
  //   LSB
  //   MSB
endmodule

module Sumador (
  input  A,
  input  B,
  input  Cin,
  output Cout,
  output S
);

  wire and_1_out, and_2_out, and_3_out, and_4_out, and_5_out, and_6_out, and_7_out, not_1_out, not_2_out,
       not_3_out, not_4_out, or_1_out, or_2_out;

  and and_1 (and_1_out, A, Cin);
  and and_2 (and_2_out, B, Cin);
  and and_3 (and_3_out, A, B);
  not not_1 (not_1_out, A);
  not not_2 (not_2_out, B);
  or or_1 (or_1_out, and_1_out, and_2_out);
  and and_4 (and_4_out, not_1_out, B);
  and and_5 (and_5_out, A, not_2_out);
  or or_2 (or_2_out, and_4_out, and_5_out);
  or or_3 (Cout, or_1_out, and_3_out);
  not not_3 (not_3_out, or_2_out);
  and and_6 (and_6_out, not_3_out, Cin);
  and and_7 (and_7_out, or_2_out, not_4_out);
  not not_4 (not_4_out, Cin);
  or or_4 (S, and_6_out, and_7_out);
endmodule
