// Logisim project Problema2-PROM.circ as structural Verilog: 1 circuit, main circuit main
module main (
  input  Binario,
  input  B2,
  input  B1,
  input  B0,
  output Gray,
  output G2,
  output G1,
  output G0
);

  wire and_1_out, and_2_out, and_3_out, and_4_out, and_5_out, and_6_out, and_7_out, and_8_out, and_9_out,
       and_10_out, and_11_out, and_12_out, and_13_out, and_14_out, and_15_out, and_16_out, not_1_out,
       not_2_out, not_3_out, not_4_out;

  not not_1 (not_1_out, Binario);
  not not_2 (not_2_out, B1);
  not not_3 (not_3_out, B2);
  not not_4 (not_4_out, B0);
  and and_1 (and_1_out, not_4_out, not_2_out, not_3_out, not_1_out);
  and and_2 (and_2_out, B0, not_2_out, not_3_out, not_1_out);
  and and_3 (and_3_out, not_4_out, B1, not_3_out, not_1_out);
  and and_4 (and_4_out, B0, B1, not_3_out, not_1_out);
  and and_5 (and_5_out, not_4_out, not_2_out, B2, not_1_out);
  and and_6 (and_6_out, B0, not_2_out, B2, not_1_out);
  and and_7 (and_7_out, not_4_out, B1, B2, not_1_out);
  and and_8 (and_8_out, B0, B1, B2, not_1_out);
  and and_9 (and_9_out, not_4_out, not_2_out, not_3_out, Binario);
  and and_10 (and_10_out, B0, not_2_out, not_3_out, Binario);
  and and_11 (and_11_out, not_4_out, B1, not_3_out, Binario);
  and and_12 (and_12_out, B0, B1, not_3_out, Binario);
  and and_13 (and_13_out, not_4_out, not_2_out, B2, Binario);
  and and_14 (and_14_out, B0, not_2_out, B2, Binario);
  and and_15 (and_15_out, not_4_out, B1, B2, Binario);
  and and_16 (and_16_out, B0, B1, B2, Binario);
  or or_1 (Gray, and_16_out, and_15_out, and_14_out, and_13_out, and_12_out, and_11_out, and_10_out, and_9_out);
  or or_2 (G2, and_12_out, and_11_out, and_10_out, and_9_out, and_8_out, and_7_out, and_6_out, and_5_out);
  or or_3 (G1, and_14_out, and_13_out, and_12_out, and_11_out, and_6_out, and_5_out, and_4_out, and_3_out);
  or or_4 (G0, and_15_out, and_14_out, and_11_out, and_10_out, and_7_out, and_6_out, and_3_out, and_2_out);

  // Notes on the sheet:
  //   B3
  //   G3
endmodule
