// Logisim project Problema03-Reconocedor_de_bits.circ as structural Verilog: 1 circuit, main circuit main
module main (
  input  X,
  output Z
);

  wire and_1_out, and_2_out, button_1_out, d_ff_1_q, d_ff_2_q, d_ff_2_qn, not_1_out, or_1_out;

  not not_1 (not_1_out, X);
  and and_1 (and_1_out, d_ff_1_q, d_ff_2_qn, X);
  and and_2 (and_2_out, not_1_out, d_ff_2_q);
  or or_1 (or_1_out, and_1_out, and_2_out);
  D_Flip_Flop d_ff_1 (.D(or_1_out), .Q(d_ff_1_q), .preset(1'b0), .en(1'b1), .reset(button_1_out));  // open: clk, Qn
  D_Flip_Flop d_ff_2 (
    .D(X), .Q(d_ff_2_q), .Qn(d_ff_2_qn), .preset(1'b0), .en(1'b1), .reset(button_1_out));  // open: clk
  Button button_1 (.out(button_1_out));
  and and_3 (Z, d_ff_1_q, d_ff_2_qn, X);

  // Notes on the sheet:
  //   Este circuito es solo una representación (no es funcional)
  //   D1
  //   D0
  //   Reset
endmodule
