// Logisim project Problema04-Circuito_Secuencial.circ as structural Verilog: 1 circuit, main circuit main
module main (
  output [2:0] out_1
);

  wire button_1_out, clock_1_out, multiplexer_3_out;
  wire [1:0] multiplexer_1_out;
  wire [1:1] d_ff_1_qn, d_ff_3_qn;

  Multiplexer #(.select(2)) multiplexer_1 (
    .in0(1'b0), .in1(1'b0), .in2(1'b0), .in3(1'b1), .out(multiplexer_1_out[0]),
    .sel({d_ff_1_qn[1], out_1[1]}), .en(1'b1));
  Multiplexer #(.select(2)) multiplexer_2 (
    .in0(1'b0), .in1(1'b0), .in2(1'b0), .in3(1'b1), .out(multiplexer_1_out[1]),
    .sel({d_ff_3_qn[1], out_1[0]}), .en(1'b1));
  Clock clock_1 (.out(clock_1_out));
  Multiplexer #(.select(2)) multiplexer_3 (
    .in0(1'b0), .in1(1'b1), .in2(1'b1), .in3(1'b1), .out(multiplexer_3_out), .sel(multiplexer_1_out),
    .en(1'b1));
  D_Flip_Flop d_ff_1 (
    .clk(clock_1_out), .D(out_1[1]), .Q(out_1[0]), .Qn(d_ff_1_qn[1]), .preset(1'b0), .en(1'b1),
    .reset(button_1_out));
  D_Flip_Flop d_ff_2 (
    .clk(clock_1_out), .D(d_ff_3_qn[1]), .Q(out_1[1]), .preset(1'b0), .en(1'b1), .reset(button_1_out));  // open: Qn
  D_Flip_Flop d_ff_3 (
    .clk(clock_1_out), .D(multiplexer_3_out), .Q(out_1[2]), .Qn(d_ff_3_qn[1]), .preset(1'b0), .en(1'b1),
    .reset(button_1_out));
  Button button_1 (.out(button_1_out));

  // Notes on the sheet:
  //   P. AND
  //   P. AND
  //   P. OR
  //   D2
  //   D1
  //   D0
  //   Reset
endmodule
