// Logisim project Anti_Mantener_Pulsado.circ as structural Verilog: 1 circuit, main circuit main
module main (
  input  IN,
  output OUT
);

  wire CLK_out, D1_q, D2_q, D3_q, not_1_out, RESET_out;

  Clock CLK (.out(CLK_out));
  D_Flip_Flop D1 (.clk(CLK_out), .D(IN), .Q(D1_q), .preset(1'b0), .en(1'b1), .reset(RESET_out));  // open: Qn
  D_Flip_Flop D2 (.clk(CLK_out), .D(D1_q), .Q(D2_q), .preset(1'b0), .en(1'b1), .reset(RESET_out));  // open: Qn
  Button RESET (.out(RESET_out));
  D_Flip_Flop D3 (.clk(CLK_out), .D(D2_q), .Q(D3_q), .preset(1'b0), .en(1'b1), .reset(RESET_out));  // open: Qn
  and and_1 (OUT, D2_q, not_1_out);
  not not_1 (not_1_out, D3_q);

  // Notes on the sheet:
  //   Retardo
  //   Almacena el valor
  //   r1
  //   r2
  //   r3
  //   Contrasta el valor actual con el anterior y si son distintos la salida OUT = 1
endmodule
