// Logisim project Cerradura-01011.circ as structural Verilog: 1 circuit, main circuit main
module main (
  input  IN,
  output Unlock
);

  wire and_1_out, and_2_out, and_3_out, and_4_out, and_5_out, and_6_out, and_7_out, clock_1_out, d_ff_1_q,
       d_ff_1_qn, d_ff_2_q, d_ff_2_qn, d_ff_3_q, d_ff_3_qn, not_1_out, or_1_out, or_2_out, or_3_out,
       RESET_out;

  not not_1 (not_1_out, IN);
  and and_1 (and_1_out, d_ff_1_q, d_ff_2_q);
  and and_2 (and_2_out, d_ff_1_q, d_ff_3_qn);
  or or_1 (or_1_out, and_6_out, and_7_out);
  and and_3 (and_3_out, d_ff_1_qn, d_ff_2_q, d_ff_3_qn, not_1_out);
  and and_4 (and_4_out, d_ff_1_q, d_ff_2_qn, d_ff_3_qn, not_1_out);
  and and_5 (and_5_out, d_ff_1_qn, d_ff_2_qn, d_ff_3_q, IN);
  and and_6 (and_6_out, IN, d_ff_3_qn, d_ff_2_qn, d_ff_1_q);
  and and_7 (and_7_out, IN, d_ff_3_q, d_ff_2_q, d_ff_1_qn);
  or or_2 (or_2_out, and_3_out, and_4_out, and_5_out);
  or or_3 (or_3_out, not_1_out, and_1_out, and_2_out);
  Clock clock_1 (.out(clock_1_out));
  D_Flip_Flop d_ff_1 (
    .clk(clock_1_out), .D(or_1_out), .Q(d_ff_1_q), .Qn(d_ff_1_qn), .preset(1'b0), .en(1'b1), .reset(RESET_out));
  D_Flip_Flop d_ff_2 (
    .clk(clock_1_out), .D(or_2_out), .Q(d_ff_2_q), .Qn(d_ff_2_qn), .preset(1'b0), .en(1'b1), .reset(RESET_out));
  D_Flip_Flop d_ff_3 (
    .clk(clock_1_out), .D(or_3_out), .Q(d_ff_3_q), .Qn(d_ff_3_qn), .preset(1'b0), .en(1'b1), .reset(RESET_out));
  Button RESET (.out(RESET_out));
  and and_8 (Unlock, d_ff_1_q, d_ff_2_qn, d_ff_3_q, IN);

  // Notes on the sheet:
  //   D2
  //   D1
  //   D0
endmodule
