// Logisim project Practica_4.circ as structural Verilog: 1 circuit, main circuit main
module main (
  output SALIDA
);

  wire B1_out, B2_out, KM1_out, or_1_out, S1_out, S2_out;

  Button B1 (.out(B1_out));
  Button B2 (.out(B2_out));
  nand S1 (S1_out, 1'b1, B1_out);
  and S2 (S2_out, S1_out, B2_out);
  and KM1 (KM1_out, or_1_out, S1_out);
  and S2_2 (SALIDA, KM1_out, S1_out);
  or or_1 (or_1_out, SALIDA, S2_out);
endmodule
