// Logisim project Practica_8.circ as structural Verilog: 4 circuits, main circuit main
module main (
  input  ON_OFF
);

  wire _0_5_2_out, _0_5_out, and_1_out, and_2_out, and_3_out, and_4_out, comparator_1_eq, comparator_1_lt,
       dec0_5_1_a, dec0_5_1_b, dec0_5_1_c, dec0_5_1_d, dec0_5_1_e, dec0_5_1_f, dec0_5_1_g, dec0_5_2_a,
       dec0_5_2_b, dec0_5_2_c, dec0_5_2_d, dec0_5_2_e, dec0_5_2_f, dec0_5_2_g, dec7seg_1_a, dec7seg_1_b,
       dec7seg_1_c, dec7seg_1_d, dec7seg_1_e, dec7seg_1_f, dec7seg_1_g, dec7seg_2_a, dec7seg_2_b,
       dec7seg_2_c, dec7seg_2_d, dec7seg_2_e, dec7seg_2_f, dec7seg_2_g, dec7seg_3_a, dec7seg_3_b,
       dec7seg_3_c, dec7seg_3_d, dec7seg_3_e, dec7seg_3_f, dec7seg_3_g, dec7seg_4_a, dec7seg_4_b,
       dec7seg_4_c, dec7seg_4_d, dec7seg_4_e, dec7seg_4_f, dec7seg_4_g, multiplexer_1_out, n0_5_1__0_5_2,
       n0_5_1_suma_resta_2, n0_5_2__0_5_2, n0_5_2_suma_resta_2, not_1_out, or_1_out, or_2_out,
       START_RESET_2_out, START_RESET_out, Suma_Resta_2_out, Suma_Resta_out;
  wire [7:0] n0_5_1_lsb, n0_5_2_lsb;

  Button Suma_Resta (.out(Suma_Resta_out));
  Button _0_5 (.out(_0_5_out));
  Button START_RESET (.out(START_RESET_out));
  LED Encendido___Suma__Apagado___Resta (.in(n0_5_1_suma_resta_2));
  Button Suma_Resta_2 (.out(Suma_Resta_2_out));
  Button _0_5_2 (.out(_0_5_2_out));
  Button START_RESET_2 (.out(START_RESET_2_out));
  LED Encendido___Suma__Apagado___Resta_2 (.in(n0_5_2_suma_resta_2));
  _0_5 u_0_5_1 (
    .Suma_Resta(Suma_Resta_out), .START_RESET(START_RESET_out), ._0_5_2(n0_5_1__0_5_2), ._0_5(_0_5_out),
    .LSB(n0_5_1_lsb[0]), .out_7(n0_5_1_lsb[1]), .out_8(n0_5_1_lsb[2]), .out_9(n0_5_1_lsb[3]),
    .out_10(n0_5_1_lsb[4]), .out_11(n0_5_1_lsb[5]), .out_12(n0_5_1_lsb[6]), .MSB(n0_5_1_lsb[7]),
    .Suma_Resta_2(n0_5_1_suma_resta_2));
  _0_5 u_0_5_2 (
    .Suma_Resta(Suma_Resta_2_out), .START_RESET(START_RESET_2_out), ._0_5_2(n0_5_2__0_5_2),
    ._0_5(_0_5_2_out), .LSB(n0_5_2_lsb[0]), .out_7(n0_5_2_lsb[1]), .out_8(n0_5_2_lsb[2]),
    .out_9(n0_5_2_lsb[3]), .out_10(n0_5_2_lsb[4]), .out_11(n0_5_2_lsb[5]), .out_12(n0_5_2_lsb[6]),
    .MSB(n0_5_2_lsb[7]), .Suma_Resta_2(n0_5_2_suma_resta_2));
  Dec7seg dec7seg_1 (
    .IN0(n0_5_1_lsb[7]), .IN1(n0_5_1_lsb[6]), .IN2(n0_5_1_lsb[5]), .A(dec7seg_1_a), .IN3(n0_5_1_lsb[4]),
    .B(dec7seg_1_b), .C(dec7seg_1_c), .D(dec7seg_1_d), .E(dec7seg_1_e), .F(dec7seg_1_f), .G(dec7seg_1_g));
  Dec7seg dec7seg_2 (
    .IN0(n0_5_1_lsb[3]), .IN1(n0_5_1_lsb[2]), .IN2(n0_5_1_lsb[1]), .A(dec7seg_2_a), .IN3(n0_5_1_lsb[0]),
    .B(dec7seg_2_b), .C(dec7seg_2_c), .D(dec7seg_2_d), .E(dec7seg_2_e), .F(dec7seg_2_f), .G(dec7seg_2_g));
  Dec0_5 dec0_5_1 (
    .in_1(n0_5_1__0_5_2), .A(dec0_5_1_a), .B(dec0_5_1_b), .C(dec0_5_1_c), .D(dec0_5_1_d), .E(dec0_5_1_e),
    .F(dec0_5_1_f), .G(dec0_5_1_g));
  _7_Segment_Display u_7_segment_display_1 (
    .g(dec7seg_1_g), .f(dec7seg_1_f), .a(dec7seg_1_a), .b(dec7seg_1_b), .e(dec7seg_1_e), .d(dec7seg_1_d),
    .c(dec7seg_1_c), .dp(1'b0));
  Comparator #(.mode("unsigned")) comparator_1 (
    .a(n0_5_1_lsb), .b(n0_5_2_lsb), .eq(comparator_1_eq), .lt(comparator_1_lt));  // open: gt
  Dec7seg dec7seg_3 (
    .IN0(n0_5_2_lsb[7]), .IN1(n0_5_2_lsb[6]), .IN2(n0_5_2_lsb[5]), .A(dec7seg_3_a), .IN3(n0_5_2_lsb[4]),
    .B(dec7seg_3_b), .C(dec7seg_3_c), .D(dec7seg_3_d), .E(dec7seg_3_e), .F(dec7seg_3_f), .G(dec7seg_3_g));
  Dec7seg dec7seg_4 (
    .IN0(n0_5_2_lsb[3]), .IN1(n0_5_2_lsb[2]), .IN2(n0_5_2_lsb[1]), .A(dec7seg_4_a), .IN3(n0_5_2_lsb[0]),
    .B(dec7seg_4_b), .C(dec7seg_4_c), .D(dec7seg_4_d), .E(dec7seg_4_e), .F(dec7seg_4_f), .G(dec7seg_4_g));
  Dec0_5 dec0_5_2 (
    .in_1(n0_5_2__0_5_2), .A(dec0_5_2_a), .B(dec0_5_2_b), .C(dec0_5_2_c), .D(dec0_5_2_d), .E(dec0_5_2_e),
    .F(dec0_5_2_f), .G(dec0_5_2_g));
  _7_Segment_Display u_7_segment_display_2 (
    .g(dec7seg_2_g), .f(dec7seg_2_f), .a(dec7seg_2_a), .b(dec7seg_2_b), .e(dec7seg_2_e), .d(dec7seg_2_d),
    .c(dec7seg_2_c), .dp(1'b1));
  not not_1 (not_1_out, n0_5_1__0_5_2);
  _7_Segment_Display u_7_segment_display_3 (
    .g(dec7seg_4_g), .f(dec7seg_4_f), .a(dec7seg_4_a), .b(dec7seg_4_b), .e(dec7seg_4_e), .d(dec7seg_4_d),
    .c(dec7seg_4_c), .dp(1'b1));
  _7_Segment_Display u_7_segment_display_4 (
    .g(dec7seg_3_g), .f(dec7seg_3_f), .a(dec7seg_3_a), .b(dec7seg_3_b), .e(dec7seg_3_e), .d(dec7seg_3_d),
    .c(dec7seg_3_c), .dp(1'b0));
  _7_Segment_Display u_7_segment_display_5 (
    .g(dec0_5_1_g), .f(dec0_5_1_f), .a(dec0_5_1_a), .b(dec0_5_1_b), .e(dec0_5_1_e), .d(dec0_5_1_d),
    .c(dec0_5_1_c), .dp(1'b0));
  and and_1 (and_1_out, comparator_1_eq, not_1_out, n0_5_1_suma_resta_2);
  _7_Segment_Display u_7_segment_display_6 (
    .g(dec0_5_2_g), .f(dec0_5_2_f), .a(dec0_5_2_a), .b(dec0_5_2_b), .e(dec0_5_2_e), .d(dec0_5_2_d),
    .c(dec0_5_2_c), .dp(1'b0));
  _7_Segment_Display u_7_segment_display_7 (
    .g(1'b1), .f(1'b1), .a(1'b1), .b(1'b1), .e(1'b0), .d(1'b0), .c(1'b0), .dp(1'b0));
  _7_Segment_Display u_7_segment_display_8 (
    .g(1'b0), .f(1'b1), .a(1'b1), .b(1'b0), .e(1'b1), .d(1'b1), .c(1'b0), .dp(1'b0));
  and and_2 (and_2_out, comparator_1_eq, not_1_out);
  and and_3 (and_3_out, comparator_1_eq, n0_5_1_suma_resta_2);
  or or_1 (or_1_out, and_1_out, comparator_1_lt);
  _7_Segment_Display u_7_segment_display_9 (
    .g(1'b1), .f(1'b1), .a(1'b1), .b(1'b1), .e(1'b0), .d(1'b0), .c(1'b0), .dp(1'b0));
  or or_2 (or_2_out, and_2_out, comparator_1_lt, and_3_out);
  _7_Segment_Display u_7_segment_display_10 (
    .g(1'b0), .f(1'b1), .a(1'b1), .b(1'b0), .e(1'b1), .d(1'b1), .c(1'b0), .dp(1'b0));
  Multiplexer multiplexer_1 (.in0(or_1_out), .in1(or_2_out), .out(multiplexer_1_out), .sel(n0_5_2__0_5_2));  // open: en
  and and_4 (and_4_out, multiplexer_1_out, ON_OFF);
  LED Sistema_de_bombeo (.in(and_4_out));

  // Notes on the sheet:
  //   TEMPERATURA DE CONSIGNA:
endmodule

module _0_5 (
  input  Suma_Resta,
  input  _0_5,
  input  START_RESET,
  output _0_5_2,
  output Suma_Resta_2,
  output LSB,
  output out_7,
  output out_8,
  output out_9,
  output out_10,
  output out_11,
  output out_12,
  output MSB
);

  wire adder_1_cout, adder_1_out, adder_2_cout, adder_2_out, adder_3_cout, adder_3_out, adder_4_out,
       adder_5_cout, adder_5_out, adder_6_cout, adder_6_out, adder_7_cout, adder_7_out, adder_8_out,
       and_1_out, and_2_out, and_3_out, and_4_out, and_5_out, and_6_out, and_7_out, d_ff_1_qn, d_ff_2_q,
       d_ff_2_qn, d_ff_3_qn, d_ff_4_qn, d_ff_5_qn, d_ff_7_qn, d_ff_9_qn, not_1_out, or_1_out, or_2_out,
       or_3_out, or_4_out, or_5_out, or_6_out, or_7_out, subtractor_1_bout, subtractor_1_out,
       subtractor_2_bout, subtractor_2_out, subtractor_3_bout, subtractor_3_out, subtractor_4_bout,
       subtractor_4_out, subtractor_5_bout, subtractor_5_out, subtractor_6_bout, subtractor_6_out,
       subtractor_7_bout, subtractor_7_out, subtractor_8_out;

  D_Flip_Flop d_ff_1 (.clk(_0_5), .D(d_ff_1_qn), .Q(_0_5_2), .Qn(d_ff_1_qn), .reset(or_4_out));  // open: preset, en
  D_Flip_Flop d_ff_2 (
    .clk(Suma_Resta), .D(d_ff_2_qn), .Q(d_ff_2_q), .Qn(d_ff_2_qn), .reset(or_4_out));  // open: preset, en
  or or_1 (or_1_out, and_2_out, and_3_out);
  D_Flip_Flop d_ff_3 (
    .clk(_0_5), .D(subtractor_1_out), .Q(LSB), .Qn(d_ff_3_qn), .preset(and_6_out), .en(or_1_out),
    .reset(or_4_out));
  D_Flip_Flop d_ff_4 (
    .clk(_0_5), .D(subtractor_2_out), .Q(out_7), .Qn(d_ff_4_qn), .en(or_1_out), .reset(or_2_out));  // open: preset
  or or_2 (or_2_out, and_6_out, or_4_out);
  D_Flip_Flop d_ff_5 (
    .clk(_0_5), .D(subtractor_3_out), .Q(out_8), .Qn(d_ff_5_qn), .en(or_1_out), .reset(or_3_out));  // open: preset
  or or_3 (or_3_out, and_6_out, or_4_out);
  D_Flip_Flop d_ff_6 (
    .clk(_0_5), .D(subtractor_4_out), .Q(out_9), .preset(and_6_out), .en(or_1_out), .reset(or_4_out));  // open: Qn
  or or_4 (or_4_out, or_7_out, and_1_out);
  and and_1 (and_1_out, out_7, d_ff_3_qn, d_ff_5_qn, out_9, Suma_Resta_2);
  D_Flip_Flop d_ff_7 (
    .clk(_0_5), .D(subtractor_5_out), .Q(out_10), .Qn(d_ff_7_qn), .preset(and_7_out), .en(or_1_out),
    .reset(or_7_out));
  D_Flip_Flop d_ff_8 (
    .clk(_0_5), .D(subtractor_6_out), .Q(out_11), .en(or_1_out), .reset(or_5_out));  // open: Qn, preset
  or or_5 (or_5_out, and_7_out, or_7_out);
  D_Flip_Flop d_ff_9 (
    .clk(_0_5), .D(subtractor_7_out), .Q(out_12), .Qn(d_ff_9_qn), .en(or_1_out), .reset(or_6_out));  // open: preset
  or or_6 (or_6_out, and_7_out, or_7_out);
  D_Flip_Flop d_ff_10 (
    .clk(_0_5), .D(subtractor_8_out), .Q(MSB), .preset(and_7_out), .en(or_1_out), .reset(or_7_out));  // open: Qn
  or or_7 (or_7_out, START_RESET, and_4_out);
  and and_2 (and_2_out, not_1_out, d_ff_2_q);
  and and_3 (and_3_out, _0_5_2, Suma_Resta_2);
  and and_4 (and_4_out, MSB, d_ff_9_qn, out_11, d_ff_7_qn);
  not not_1 (not_1_out, _0_5_2);
  and and_5 (and_5_out, LSB, d_ff_4_qn, d_ff_5_qn, out_9, Suma_Resta_2);
  and and_6 (and_6_out, LSB, out_7, out_8, out_9, d_ff_2_q);
  and and_7 (and_7_out, out_10, out_11, out_12, MSB, d_ff_2_q);
  Adder #(.width(1)) adder_1 (.a(LSB), .b(1'b0), .out(adder_1_out), .cin(Suma_Resta_2), .cout(adder_1_cout));
  Adder #(.width(1)) adder_2 (.a(out_7), .b(1'b0), .out(adder_2_out), .cin(adder_1_cout), .cout(adder_2_cout));
  Adder #(.width(1)) adder_3 (.a(out_8), .b(1'b0), .out(adder_3_out), .cin(adder_2_cout), .cout(adder_3_cout));
  Adder #(.width(1)) adder_4 (.a(out_9), .b(1'b0), .out(adder_4_out), .cin(adder_3_cout));  // open: cout
  Adder #(.width(1)) adder_5 (.a(out_10), .b(1'b0), .out(adder_5_out), .cin(and_5_out), .cout(adder_5_cout));
  Adder #(.width(1)) adder_6 (.a(out_11), .b(1'b0), .out(adder_6_out), .cin(adder_5_cout), .cout(adder_6_cout));
  Adder #(.width(1)) adder_7 (.a(out_12), .b(1'b0), .out(adder_7_out), .cin(adder_6_cout), .cout(adder_7_cout));
  Adder #(.width(1)) adder_8 (.a(MSB), .b(1'b0), .out(adder_8_out), .cin(adder_7_cout));  // open: cout
  not not_2 (Suma_Resta_2, d_ff_2_q);
  Subtractor #(.width(1)) subtractor_1 (
    .a(adder_1_out), .b(1'b0), .out(subtractor_1_out), .bin(d_ff_2_q), .bout(subtractor_1_bout));
  Subtractor #(.width(1)) subtractor_2 (
    .a(adder_2_out), .b(1'b0), .out(subtractor_2_out), .bin(subtractor_1_bout), .bout(subtractor_2_bout));
  Subtractor #(.width(1)) subtractor_3 (
    .a(adder_3_out), .b(1'b0), .out(subtractor_3_out), .bin(subtractor_2_bout), .bout(subtractor_3_bout));
  Subtractor #(.width(1)) subtractor_4 (
    .a(adder_4_out), .b(1'b0), .out(subtractor_4_out), .bin(subtractor_3_bout), .bout(subtractor_4_bout));
  Subtractor #(.width(1)) subtractor_5 (
    .a(adder_5_out), .b(1'b0), .out(subtractor_5_out), .bin(subtractor_4_bout), .bout(subtractor_5_bout));
  Subtractor #(.width(1)) subtractor_6 (
    .a(adder_6_out), .b(1'b0), .out(subtractor_6_out), .bin(subtractor_5_bout), .bout(subtractor_6_bout));
  Subtractor #(.width(1)) subtractor_7 (
    .a(adder_7_out), .b(1'b0), .out(subtractor_7_out), .bin(subtractor_6_bout), .bout(subtractor_7_bout));
  Subtractor #(.width(1)) subtractor_8 (
    .a(adder_8_out), .b(1'b0), .out(subtractor_8_out), .bin(subtractor_7_bout));  // open: bout
endmodule

module Dec0_5 (
  input  in_1,
  output A,
  output B,
  output C,
  output D,
  output E,
  output F,
  output G
);

  not not_1 (B, in_1);
  not not_2 (E, in_1);
  _7_Segment_Display u_7_segment_display_1 (.g(in_1), .f(1'b1), .a(1'b1), .b(B), .e(E), .d(1'b1), .c(1'b1), .dp(1'b0));

  assign A = 1'b1;
  assign C = 1'b1;
  assign D = 1'b1;
  assign F = 1'b1;
  assign G = in_1;
endmodule

module Dec7seg (
  input  IN0,
  input  IN1,
  input  IN2,
  input  IN3,
  output A,
  output B,
  output C,
  output D,
  output E,
  output F,
  output G
);

  wire and_1_out, and_2_out, and_3_out, and_4_out, and_5_out, and_6_out, and_7_out, and_8_out, and_9_out,
       and_10_out, and_11_out, and_12_out, and_13_out, and_14_out, and_15_out, and_16_out, and_17_out,
       and_18_out, and_19_out, and_20_out, and_21_out, and_22_out, and_23_out, and_24_out, and_25_out,
       and_26_out, and_27_out, and_28_out, and_29_out, and_30_out, and_31_out, and_32_out, and_33_out,
       and_34_out, and_35_out, not_1_out, not_2_out, not_3_out, not_4_out, not_5_out, not_6_out, not_7_out,
       not_8_out, not_9_out, not_10_out, not_11_out, not_12_out, not_13_out, not_14_out, not_15_out,
       not_16_out, not_17_out, not_18_out, not_19_out, not_20_out, not_21_out, not_22_out, not_23_out,
       not_24_out, not_25_out, not_26_out, not_27_out, not_28_out, not_29_out, not_30_out, not_31_out,
       not_32_out, not_33_out, not_34_out, not_35_out, not_36_out, not_37_out, not_38_out, not_39_out,
       not_40_out, not_41_out, not_42_out, not_43_out;

  not not_1 (not_1_out, IN1);
  and and_1 (and_1_out, not_1_out, not_2_out);
  not not_2 (not_2_out, IN3);
  not not_3 (not_3_out, IN0);
  and and_2 (and_2_out, not_3_out, IN2);
  not not_4 (not_4_out, IN0);
  and and_3 (and_3_out, not_4_out, IN1, IN3);
  and and_4 (and_4_out, IN1, IN2);
  not not_5 (not_5_out, IN1);
  and and_5 (and_5_out, IN0, not_5_out, not_6_out);
  not not_6 (not_6_out, IN2);
  and and_6 (and_6_out, IN0, not_7_out);
  not not_7 (not_7_out, IN3);
  not not_8 (not_8_out, IN0);
  and and_7 (and_7_out, not_8_out, not_9_out);
  not not_9 (not_9_out, IN1);
  not not_10 (not_10_out, IN0);
  and and_8 (and_8_out, not_10_out, not_11_out, not_12_out);
  not not_11 (not_11_out, IN2);
  not not_12 (not_12_out, IN3);
  not not_13 (not_13_out, IN1);
  and and_9 (and_9_out, not_13_out, not_14_out);
  not not_14 (not_14_out, IN3);
  not not_15 (not_15_out, IN0);
  and and_10 (and_10_out, not_15_out, IN2, IN3);
  not not_16 (not_16_out, IN2);
  and and_11 (and_11_out, IN0, not_16_out, IN3);
  not not_17 (not_17_out, IN0);
  and and_12 (and_12_out, not_17_out, not_18_out);
  not not_18 (not_18_out, IN2);
  not not_19 (not_19_out, IN0);
  and and_13 (and_13_out, not_19_out, IN3);
  not not_20 (not_20_out, IN2);
  and and_14 (and_14_out, not_20_out, IN3);
  not not_21 (not_21_out, IN0);
  and and_15 (and_15_out, not_21_out, IN1);
  and and_16 (and_16_out, IN0, not_22_out);
  not not_22 (not_22_out, IN1);
  not not_23 (not_23_out, IN0);
  and and_17 (and_17_out, not_23_out, not_24_out, not_25_out);
  not not_24 (not_24_out, IN1);
  not not_25 (not_25_out, IN3);
  not not_26 (not_26_out, IN1);
  and and_18 (and_18_out, not_26_out, IN2, IN3);
  not not_27 (not_27_out, IN2);
  and and_19 (and_19_out, IN1, not_27_out, IN3);
  and and_20 (and_20_out, IN1, IN2, not_28_out);
  not not_28 (not_28_out, IN3);
  and and_21 (and_21_out, IN0, not_29_out);
  not not_29 (not_29_out, IN2);
  not not_30 (not_30_out, IN1);
  and and_22 (and_22_out, not_30_out, not_31_out);
  not not_31 (not_31_out, IN3);
  and and_23 (and_23_out, IN2, not_32_out);
  not not_32 (not_32_out, IN3);
  and and_24 (and_24_out, IN0, IN2);
  and and_25 (and_25_out, IN0, IN1);
  not not_33 (not_33_out, IN2);
  and and_26 (and_26_out, not_33_out, not_34_out);
  not not_34 (not_34_out, IN3);
  not not_35 (not_35_out, IN0);
  and and_27 (and_27_out, not_35_out, IN1, not_36_out);
  not not_36 (not_36_out, IN2);
  and and_28 (and_28_out, IN1, not_37_out);
  not not_37 (not_37_out, IN3);
  and and_29 (and_29_out, IN0, not_38_out);
  not not_38 (not_38_out, IN1);
  and and_30 (and_30_out, IN0, IN2);
  not not_39 (not_39_out, IN1);
  and and_31 (and_31_out, not_39_out, IN2);
  and and_32 (and_32_out, IN2, not_40_out);
  not not_40 (not_40_out, IN3);
  not not_41 (not_41_out, IN0);
  and and_33 (and_33_out, not_41_out, IN1, not_42_out);
  not not_42 (not_42_out, IN2);
  and and_34 (and_34_out, IN0, not_43_out);
  not not_43 (not_43_out, IN1);
  and and_35 (and_35_out, IN0, IN3);
  or or_1 (B, and_7_out, and_8_out, and_9_out, and_10_out, and_11_out);
  or or_2 (C, and_12_out, and_13_out, and_14_out, and_15_out, and_16_out);
  or or_3 (D, and_17_out, and_18_out, and_19_out, and_20_out, and_21_out);
  or or_4 (E, and_22_out, and_23_out, and_24_out, and_25_out);
  or or_5 (F, and_26_out, and_27_out, and_28_out, and_29_out, and_30_out);
  or or_6 (G, and_31_out, and_32_out, and_33_out, and_34_out, and_35_out);
  or or_7 (A, and_1_out, and_2_out, and_3_out, and_4_out, and_5_out, and_6_out);
endmodule
