// Logisim project Puerta_Almacen.circ as structural Verilog: 1 circuit, main circuit main
module main (
  input  Abrir_puerta,
  input  Sensor_final_de_carrera,
  input  Cerrar_puerta,
  input  Fotocelula,
  output Abre_puerta,
  output Cierra_puerta
);

  wire nand_1_out, nand_2_out, nand_4_out, nand_5_out;

  nand nand_1 (nand_1_out, Sensor_final_de_carrera, Cerrar_puerta);
  nand nand_2 (nand_2_out, Abrir_puerta, Sensor_final_de_carrera);
  nand nand_3 (Abre_puerta, nand_2_out, nand_2_out);
  nand nand_4 (nand_4_out, nand_1_out, nand_1_out);
  nand nand_5 (nand_5_out, nand_4_out, Fotocelula);
  nand nand_6 (Cierra_puerta, nand_5_out, nand_5_out);
endmodule
